// Logisim project contador.circ as structural Verilog: 1 circuit, main circuit main
module main (
  input  in_1,
  input  in_2,
  output [7:0] out_3
);

  wire clock_1_out;

  Clock clock_1 (.out(clock_1_out));
  J_K_Flip_Flop #(.trigger("falling")) j_k_ff_1 (
    .J(in_1), .clk(clock_1_out), .K(in_1), .Q(out_3[0]), .reset(in_2));  // open: Qn, preset, en
  J_K_Flip_Flop #(.trigger("falling")) j_k_ff_2 (
    .J(in_1), .clk(out_3[0]), .K(in_1), .Q(out_3[1]), .reset(in_2));  // open: Qn, preset, en
  J_K_Flip_Flop #(.trigger("falling")) j_k_ff_3 (
    .J(in_1), .clk(out_3[1]), .K(in_1), .Q(out_3[2]), .reset(in_2));  // open: Qn, preset, en
  J_K_Flip_Flop #(.trigger("falling")) j_k_ff_4 (
    .J(in_1), .clk(out_3[2]), .K(in_1), .Q(out_3[3]), .reset(in_2));  // open: Qn, preset, en
  J_K_Flip_Flop #(.trigger("falling")) j_k_ff_5 (
    .J(in_1), .clk(out_3[3]), .K(in_1), .Q(out_3[4]), .reset(in_2));  // open: Qn, preset, en
  J_K_Flip_Flop #(.trigger("falling")) j_k_ff_6 (
    .J(in_1), .clk(out_3[4]), .K(in_1), .Q(out_3[5]), .reset(in_2));  // open: Qn, preset, en
  J_K_Flip_Flop #(.trigger("falling")) j_k_ff_7 (
    .J(in_1), .clk(out_3[5]), .K(in_1), .Q(out_3[6]), .reset(in_2));  // open: Qn, preset, en
  J_K_Flip_Flop #(.trigger("falling")) j_k_ff_8 (
    .J(in_1), .clk(out_3[6]), .K(in_1), .Q(out_3[7]), .reset(in_2));  // open: Qn, preset, en

  // Notes on the sheet:
  //   1
  //   2
  //   4
  //   8
  //   16
  //   32
  //   64
  //   128
endmodule
