// Logisim project mata3820172.circ as structural Verilog: 1 circuit, main circuit main
module main (
  input  in_1,
  output [7:0] S3,
  output [7:0] S2,
  output [7:0] S1,
  output [7:0] S0,
  output [1:0] out_6,
  output [1:0] out_7,
  output [7:0] out_8,
  output [7:0] out_9,
  output [7:0] out_10,
  output [7:0] out_11,
  output [7:0] out_12,
  output [7:0] out_13,
  output [7:0] out_14,
  output [7:0] out_15,
  output [7:0] out_16,
  output [7:0] out_17,
  output [7:0] out_18,
  output [7:0] out_19,
  output [7:0] out_20,
  output [7:0] out_21,
  output [7:0] out_22,
  output [7:0] out_23,
  output [7:0] out_24,
  output [7:0] out_25,
  output [7:0] out_26,
  output [3:0] out_27,
  output [7:0] out_28,
  output [7:0] out_29,
  output out_30,
  output [7:0] out_31,
  output out_32,
  output [7:0] out_33,
  output [7:0] out_34,
  output [7:0] out_35,
  output [7:0] out_36,
  output [7:0] out_37,
  output [7:0] out_38,
  output [7:0] out_39,
  output [7:0] out_40,
  output [7:0] out_41,
  output [7:0] out_42,
  output [7:0] out_43,
  output [7:0] out_44,
  output [7:0] out_45,
  output [7:0] out_46,
  output [7:0] out_47
);

  wire adder_2_cout, and_1_out, and_2_out, and_3_out, and_4_out, clock_1_out, comparator_1_eq,
       comparator_2_eq, comparator_5_eq, comparator_6_eq, comparator_7_eq, comparator_8_eq, comparator_9_eq,
       comparator_10_lt, comparator_11_gt, comparator_12_eq, comparator_12_lt, comparator_13_eq,
       comparator_13_gt, not_1_out, not_2_out, not_3_out, not_4_out, or_1_out, or_2_out, or_3_out;
  wire [7:0] adder_1_out, controlled_buffer_1_out, controlled_buffer_3_out, controlled_buffer_4_out,
       controlled_buffer_5_out, controlled_buffer_6_out, multiplexer_2_out, multiplexer_8_out, PC_q;

  not not_1 (not_1_out, comparator_2_eq);
  Adder adder_1 (.a(8'h1), .b(PC_q), .out(adder_1_out));  // open: cin, cout
  assign controlled_buffer_1_out = not_2_out ? adder_1_out : 8'bz;  // Controlled_Buffer controlled_buffer_1
  Comparator #(.width(4)) comparator_1 (.a(out_27), .b(4'b1110), .eq(comparator_1_eq));  // open: gt, lt
  Comparator #(.width(4)) comparator_2 (.a(out_27), .b(4'b1111), .eq(comparator_2_eq));  // open: gt, lt
  Comparator #(.width(4)) comparator_3 (.a(out_27), .b(4'b1011), .eq(out_30));  // open: gt, lt
  Comparator #(.width(4)) comparator_4 (.a(out_27), .b(4'b1100), .eq(out_32));  // open: gt, lt
  not not_2 (not_2_out, comparator_1_eq);
  assign controlled_buffer_1_out = comparator_1_eq ? out_16 : 8'bz;  // Controlled_Buffer controlled_buffer_2
  Register PC (.D(controlled_buffer_1_out), .en(not_1_out), .Q(PC_q), .clk(clock_1_out), .clr(in_1));
  or or_1 (or_1_out, out_30, not_3_out);
  not not_3 (not_3_out, out_32);
  RAM ram_1 (.addr(PC_q), .data({out_27, out_6, out_7}), .clk(clock_1_out));  // open: sel, ld, clr
  Clock clock_1 (.out(clock_1_out));
  Comparator #(.width(2)) comparator_5 (.a(2'b11), .b(out_7), .eq(comparator_5_eq));  // open: gt, lt
  Comparator #(.width(2)) comparator_6 (.a(2'b10), .b(out_7), .eq(comparator_6_eq));  // open: gt, lt
  Comparator #(.width(2)) comparator_7 (.a(2'b01), .b(out_7), .eq(comparator_7_eq));  // open: gt, lt
  Comparator #(.width(2)) comparator_8 (.a(2'b00), .b(out_7), .eq(comparator_8_eq));  // open: gt, lt
  RAM ram_2 (.addr(out_16), .data(out_31), .clk(clock_1_out), .ld(or_1_out));  // open: sel, clr
  and and_1 (and_1_out, out_30, comparator_5_eq);
  and and_2 (and_2_out, out_30, comparator_6_eq);
  and and_3 (and_3_out, out_30, comparator_7_eq);
  and and_4 (and_4_out, out_30, comparator_8_eq);
  assign controlled_buffer_3_out = and_1_out ? out_31 : 8'bz;  // Controlled_Buffer controlled_buffer_3
  assign controlled_buffer_4_out = and_2_out ? out_31 : 8'bz;  // Controlled_Buffer controlled_buffer_4
  assign controlled_buffer_5_out = and_3_out ? out_31 : 8'bz;  // Controlled_Buffer controlled_buffer_5
  assign controlled_buffer_6_out = and_4_out ? out_31 : 8'bz;  // Controlled_Buffer controlled_buffer_6
  not not_4 (not_4_out, and_4_out);
  assign controlled_buffer_6_out = not_4_out ? multiplexer_8_out : 8'bz;  // Controlled_Buffer controlled_buffer_7
  Register R0 (.D(controlled_buffer_6_out), .Q(S0), .clk(clock_1_out));  // open: en, clr
  Multiplexer #(.select(2), .width(8)) multiplexer_1 (
    .in0(S0), .in1(S1), .in2(S2), .in3(S3), .out(out_16), .sel(out_6));  // open: en
  Register R1 (.D(controlled_buffer_5_out), .Q(S1), .clk(clock_1_out));  // open: en, clr
  Register R2 (.D(controlled_buffer_4_out), .Q(S2), .clk(clock_1_out));  // open: en, clr
  Multiplexer #(.select(2), .width(8)) multiplexer_2 (
    .in0(S0), .in1(S1), .in2(S2), .in3(S3), .out(multiplexer_2_out), .sel(out_7));  // open: en
  Register R3 (.D(controlled_buffer_3_out), .Q(S3), .clk(clock_1_out));  // open: en, clr
  Demultiplexer #(.select(4), .width(8)) demultiplexer_1 (
    .out0(out_9), .out1(out_10), .out2(out_12), .out3(out_13), .out4(out_14), .out5(out_17), .out6(out_18),
    .out7(out_20), .out8(out_21), .out9(out_22), .out10(out_24), .out11(out_25), .out12(out_29), .in(out_16),
    .sel(out_27));  // open: out13, out14, out15, en
  Demultiplexer #(.select(4), .width(8)) demultiplexer_2 (
    .out0(out_33), .out1(out_35), .out2(out_36), .out3(out_37), .out4(out_38), .out5(out_39), .out6(out_41),
    .out7(out_42), .out8(out_43), .out9(out_44), .out10(out_45), .out15(out_37), .in(multiplexer_2_out),
    .sel(out_27));  // open: out11, out12, out13, out14, en
  Comparator #(.mode("unsigned")) comparator_9 (.a(out_18), .b(out_41), .eq(comparator_9_eq));  // open: gt, lt
  Comparator #(.mode("unsigned")) comparator_10 (.a(out_20), .b(out_42), .lt(comparator_10_lt));  // open: gt, eq
  Comparator #(.mode("unsigned")) comparator_11 (.a(out_21), .b(out_43), .gt(comparator_11_gt));  // open: eq, lt
  Comparator #(.mode("unsigned")) comparator_12 (
    .a(out_22), .b(out_44), .eq(comparator_12_eq), .lt(comparator_12_lt));  // open: gt
  Comparator #(.mode("unsigned")) comparator_13 (
    .a(out_24), .b(out_45), .gt(comparator_13_gt), .eq(comparator_13_eq));  // open: lt
  or or_2 (or_2_out, comparator_13_gt, comparator_13_eq);
  or or_3 (or_3_out, comparator_12_eq, comparator_12_lt);
  assign out_8 = out_9 & out_33;  // AND_Gate and_5, 8 bits wide
  assign out_11 = out_10 | out_35;  // OR_Gate or_4, 8 bits wide
  assign out_15 = out_12 ^ out_36;  // XOR_Gate xor_1, 8 bits wide
  assign out_19 = ~out_13;  // NOT_Gate not_5, 8 bits wide
  Adder adder_2 (.a(out_14), .b(out_38), .out(out_23), .cout(adder_2_cout));  // open: cin
  Subtractor subtractor_1 (.a(out_17), .b(out_39), .out(out_26));  // open: bin, bout
  Multiplexer #(.width(8)) multiplexer_3 (
    .in0({8{1'b0}}), .in1(8'h1), .out(out_28), .sel(comparator_9_eq));  // open: en
  Multiplexer #(.width(8)) multiplexer_4 (
    .in0({8{1'b0}}), .in1(8'h1), .out(out_34), .sel(comparator_10_lt));  // open: en
  Multiplexer #(.width(8)) multiplexer_5 (
    .in0({8{1'b0}}), .in1(8'h1), .out(out_40), .sel(comparator_11_gt));  // open: en
  Multiplexer #(.width(8)) multiplexer_6 (.in0({8{1'b0}}), .in1(8'h1), .out(out_46), .sel(or_3_out));  // open: en
  Multiplexer #(.width(8)) multiplexer_7 (.in0({8{1'b0}}), .in1(8'h1), .out(out_47), .sel(or_2_out));  // open: en
  Multiplexer #(.select(4), .width(8)) multiplexer_8 (
    .in0(out_8), .in1(out_11), .in2(out_15), .in3(out_19), .in4(out_23), .in5(out_26), .in6(out_28),
    .in7(out_34), .in8(out_40), .in9(out_46), .in10(out_47), .out(multiplexer_8_out), .sel(out_27));  // open: in11, in12, in13, in14, in15, en

  // Notes on the sheet:
  //   JMP
  //   HLT
  //   LDA
  //   STR
  //   Memória de programa
  //   Memória de dados
  //   Rx
  //   Ry
  //   Rx
  //   Ry
endmodule
