// Logisim project memoria.circ as structural Verilog: 1 circuit, main circuit main
module main (
  input  [15:0] in_1,
  input  in_2,
  input  in_3,
  input  in_4,
  input  in_5,
  input  in_6,
  input  in_7,
  input  in_8,
  input  in_9,
  input  in_10,
  input  in_11,
  input  in_12,
  input  in_13,
  input  in_14,
  input  in_15,
  input  in_16,
  input  in_17,
  input  in_18,
  input  in_19,
  input  in_20,
  output [7:0] out_21,
  output [7:0] out_22
);

  wire clock_1_out, clock_2_out, j_k_ff_1_q, j_k_ff_2_q, j_k_ff_3_q, j_k_ff_4_q, j_k_ff_5_q, j_k_ff_6_q,
       j_k_ff_7_q, j_k_ff_8_q, j_k_ff_9_q, j_k_ff_10_q, j_k_ff_11_q, j_k_ff_12_q, j_k_ff_13_q, j_k_ff_14_q,
       j_k_ff_15_q, j_k_ff_16_q, not_1_out;
  wire [15:0] bitselector_1_out, bitselector_3_out, bitselector_4_out, bitselector_5_out, bitselector_6_out,
       bitselector_7_out, bitselector_8_out, bitselector_9_out, bitselector_10_out, bitselector_11_out,
       bitselector_12_out, bitselector_13_out, bitselector_14_out, bitselector_15_out, bitselector_16_out,
       bitselector_17_out;

  Clock clock_1 (.out(clock_1_out));
  not not_1 (not_1_out, in_20);
  BitSelector #(.width(1), .group(16)) bitselector_1 (.in(j_k_ff_1_q), .out(bitselector_1_out), .sel(in_4));
  J_K_Flip_Flop #(.trigger("falling")) j_k_ff_1 (
    .J(in_20), .clk(clock_1_out), .K(in_20), .Q(j_k_ff_1_q), .reset(not_1_out));  // open: Qn, preset, en
  BitSelector #(.width(16), .group(8)) bitselector_2 (.in(in_1), .out(out_22), .sel(in_3));
  BitSelector #(.width(1), .group(16)) bitselector_3 (.in(j_k_ff_2_q), .out(bitselector_3_out), .sel(in_5));
  J_K_Flip_Flop #(.trigger("falling")) j_k_ff_2 (
    .J(in_20), .clk(j_k_ff_1_q), .K(in_20), .Q(j_k_ff_2_q), .reset(not_1_out));  // open: Qn, preset, en
  J_K_Flip_Flop #(.trigger("falling")) j_k_ff_3 (
    .J(in_20), .clk(j_k_ff_2_q), .K(in_20), .Q(j_k_ff_3_q), .reset(not_1_out));  // open: Qn, preset, en
  BitSelector #(.width(1), .group(16)) bitselector_4 (.in(j_k_ff_3_q), .out(bitselector_4_out), .sel(in_6));
  BitSelector #(.width(1), .group(16)) bitselector_5 (.in(j_k_ff_4_q), .out(bitselector_5_out), .sel(in_7));
  J_K_Flip_Flop #(.trigger("falling")) j_k_ff_4 (
    .J(in_20), .clk(j_k_ff_3_q), .K(in_20), .Q(j_k_ff_4_q), .reset(not_1_out));  // open: Qn, preset, en
  BitSelector #(.width(1), .group(16)) bitselector_6 (.in(j_k_ff_5_q), .out(bitselector_6_out), .sel(in_8));
  J_K_Flip_Flop #(.trigger("falling")) j_k_ff_5 (
    .J(in_20), .clk(j_k_ff_4_q), .K(in_20), .Q(j_k_ff_5_q), .reset(not_1_out));  // open: Qn, preset, en
  Clock clock_2 (.out(clock_2_out));
  BitSelector #(.width(1), .group(16)) bitselector_7 (.in(j_k_ff_6_q), .out(bitselector_7_out), .sel(in_9));
  J_K_Flip_Flop #(.trigger("falling")) j_k_ff_6 (
    .J(in_20), .clk(j_k_ff_5_q), .K(in_20), .Q(j_k_ff_6_q), .reset(not_1_out));  // open: Qn, preset, en
  RAM #(.addrWidth(16), .bus("separate")) ram_1 (
    .addr(in_1), .din(out_22), .data(out_21));  // open: str, sel, clk, ld, clr
  BitSelector #(.width(1), .group(16)) bitselector_8 (.in(j_k_ff_7_q), .out(bitselector_8_out), .sel(in_10));
  J_K_Flip_Flop #(.trigger("falling")) j_k_ff_7 (
    .J(in_20), .clk(j_k_ff_6_q), .K(in_20), .Q(j_k_ff_7_q), .reset(not_1_out));  // open: Qn, preset, en
  J_K_Flip_Flop #(.trigger("falling")) j_k_ff_8 (
    .J(in_20), .clk(j_k_ff_7_q), .K(in_20), .Q(j_k_ff_8_q), .reset(not_1_out));  // open: Qn, preset, en
  BitSelector #(.width(1), .group(16)) bitselector_9 (.in(j_k_ff_8_q), .out(bitselector_9_out), .sel(in_11));
  J_K_Flip_Flop #(.trigger("falling")) j_k_ff_9 (
    .J(in_20), .clk(j_k_ff_8_q), .K(in_20), .Q(j_k_ff_9_q), .reset(not_1_out));  // open: Qn, preset, en
  BitSelector #(.width(1), .group(16)) bitselector_10 (.in(j_k_ff_9_q), .out(bitselector_10_out), .sel(in_12));
  BitSelector #(.width(1), .group(16)) bitselector_11 (.in(j_k_ff_10_q), .out(bitselector_11_out), .sel(in_13));
  J_K_Flip_Flop #(.trigger("falling")) j_k_ff_10 (
    .J(in_20), .clk(j_k_ff_9_q), .K(in_20), .Q(j_k_ff_10_q), .reset(not_1_out));  // open: Qn, preset, en
  BitSelector #(.width(1), .group(16)) bitselector_12 (.in(j_k_ff_11_q), .out(bitselector_12_out), .sel(in_14));
  J_K_Flip_Flop #(.trigger("falling")) j_k_ff_11 (
    .J(in_20), .clk(j_k_ff_10_q), .K(in_20), .Q(j_k_ff_11_q), .reset(not_1_out));  // open: Qn, preset, en
  BitSelector #(.width(1), .group(16)) bitselector_13 (.in(j_k_ff_12_q), .out(bitselector_13_out), .sel(in_15));
  J_K_Flip_Flop #(.trigger("falling")) j_k_ff_12 (
    .J(in_20), .clk(j_k_ff_11_q), .K(in_20), .Q(j_k_ff_12_q), .reset(not_1_out));  // open: Qn, preset, en
  BitSelector #(.width(1), .group(16)) bitselector_14 (.in(j_k_ff_13_q), .out(bitselector_14_out), .sel(in_16));
  J_K_Flip_Flop #(.trigger("falling")) j_k_ff_13 (
    .J(in_20), .clk(j_k_ff_12_q), .K(in_20), .Q(j_k_ff_13_q), .reset(not_1_out));  // open: Qn, preset, en
  BitSelector #(.width(1), .group(16)) bitselector_15 (.in(j_k_ff_14_q), .out(bitselector_15_out), .sel(in_17));
  J_K_Flip_Flop #(.trigger("falling")) j_k_ff_14 (
    .J(in_20), .clk(j_k_ff_13_q), .K(in_20), .Q(j_k_ff_14_q), .reset(not_1_out));  // open: Qn, preset, en
  J_K_Flip_Flop #(.trigger("falling")) j_k_ff_15 (
    .J(in_20), .clk(j_k_ff_14_q), .K(in_20), .Q(j_k_ff_15_q), .reset(not_1_out));  // open: Qn, preset, en
  BitSelector #(.width(1), .group(16)) bitselector_16 (.in(j_k_ff_15_q), .out(bitselector_16_out), .sel(in_18));
  BitSelector #(.width(1), .group(16)) bitselector_17 (.in(j_k_ff_16_q), .out(bitselector_17_out), .sel(in_19));
  J_K_Flip_Flop #(.trigger("falling")) j_k_ff_16 (
    .J(in_20), .clk(j_k_ff_15_q), .K(in_20), .Q(j_k_ff_16_q), .reset(not_1_out));  // open: Qn, preset, en

  // Notes on the sheet:
  //   endereçamento
  //   entrada de dados
endmodule
